// Digital circuit 1 x 1 RAM.dig as structural Verilog
module _1_x_1_RAM (
  input  WD,
  input  WS,
  input  RS1,
  input  RS2,
  input  Clk,
  output RD1,
  output RD2
);

  wire d_ff_1_q, multiplexer_1_out;

  Multiplexer multiplexer_1 (.sel(WS), .in_0(d_ff_1_q), .in_1(WD), .out(multiplexer_1_out));
  D_FF d_ff_1 (.D(multiplexer_1_out), .C(Clk), .Q(d_ff_1_q));  // open: nQ
  and and_1 (RD1, RS1, d_ff_1_q);
  and and_2 (RD2, RS2, d_ff_1_q);
endmodule
