// Digital circuit 1 x 15 RAM.dig as structural Verilog
module _1_x_15_RAM (
  input  RS1,
  input  RS2,
  input  WS,
  input  [14:0] WD_14_0,
  input  Clk,
  output [14:0] RD1_14_0,
  output [14:0] RD2_14_0
);

  _1_x_1_RAM _1_x_1_ram_1 (
    .WD(WD_14_0[14]), .WS(WS), .RS1(RS1), .RS2(RS2), .Clk(Clk), .RD1(RD1_14_0[14]), .RD2(RD2_14_0[14]));
  _1_x_1_RAM _1_x_1_ram_2 (
    .WD(WD_14_0[11]), .WS(WS), .RS1(RS1), .RS2(RS2), .Clk(Clk), .RD1(RD1_14_0[11]), .RD2(RD2_14_0[11]));
  _1_x_1_RAM _1_x_1_ram_3 (
    .WD(WD_14_0[8]), .WS(WS), .RS1(RS1), .RS2(RS2), .Clk(Clk), .RD1(RD1_14_0[8]), .RD2(RD2_14_0[8]));
  _1_x_1_RAM _1_x_1_ram_4 (
    .WD(WD_14_0[5]), .WS(WS), .RS1(RS1), .RS2(RS2), .Clk(Clk), .RD1(RD1_14_0[5]), .RD2(RD2_14_0[5]));
  _1_x_1_RAM _1_x_1_ram_5 (
    .WD(WD_14_0[2]), .WS(WS), .RS1(RS1), .RS2(RS2), .Clk(Clk), .RD1(RD1_14_0[2]), .RD2(RD2_14_0[2]));
  _1_x_1_RAM _1_x_1_ram_6 (
    .WD(WD_14_0[13]), .WS(WS), .RS1(RS1), .RS2(RS2), .Clk(Clk), .RD1(RD1_14_0[13]), .RD2(RD2_14_0[13]));
  _1_x_1_RAM _1_x_1_ram_7 (
    .WD(WD_14_0[10]), .WS(WS), .RS1(RS1), .RS2(RS2), .Clk(Clk), .RD1(RD1_14_0[10]), .RD2(RD2_14_0[10]));
  _1_x_1_RAM _1_x_1_ram_8 (
    .WD(WD_14_0[7]), .WS(WS), .RS1(RS1), .RS2(RS2), .Clk(Clk), .RD1(RD1_14_0[7]), .RD2(RD2_14_0[7]));
  _1_x_1_RAM _1_x_1_ram_9 (
    .WD(WD_14_0[4]), .WS(WS), .RS1(RS1), .RS2(RS2), .Clk(Clk), .RD1(RD1_14_0[4]), .RD2(RD2_14_0[4]));
  _1_x_1_RAM _1_x_1_ram_10 (
    .WD(WD_14_0[1]), .WS(WS), .RS1(RS1), .RS2(RS2), .Clk(Clk), .RD1(RD1_14_0[1]), .RD2(RD2_14_0[1]));
  _1_x_1_RAM _1_x_1_ram_11 (
    .WD(WD_14_0[12]), .WS(WS), .RS1(RS1), .RS2(RS2), .Clk(Clk), .RD1(RD1_14_0[12]), .RD2(RD2_14_0[12]));
  _1_x_1_RAM _1_x_1_ram_12 (
    .WD(WD_14_0[9]), .WS(WS), .RS1(RS1), .RS2(RS2), .Clk(Clk), .RD1(RD1_14_0[9]), .RD2(RD2_14_0[9]));
  _1_x_1_RAM _1_x_1_ram_13 (
    .WD(WD_14_0[6]), .WS(WS), .RS1(RS1), .RS2(RS2), .Clk(Clk), .RD1(RD1_14_0[6]), .RD2(RD2_14_0[6]));
  _1_x_1_RAM _1_x_1_ram_14 (
    .WD(WD_14_0[3]), .WS(WS), .RS1(RS1), .RS2(RS2), .Clk(Clk), .RD1(RD1_14_0[3]), .RD2(RD2_14_0[3]));
  _1_x_1_RAM _1_x_1_ram_15 (
    .WD(WD_14_0[0]), .WS(WS), .RS1(RS1), .RS2(RS2), .Clk(Clk), .RD1(RD1_14_0[0]), .RD2(RD2_14_0[0]));

  // Other names for the same wires on the sheet: R0 = RD2_14_0[0]; R1 = RD2_14_0[1]; R2 = RD2_14_0[2];
  //   R3 = RD2_14_0[3]; R4 = RD2_14_0[4]; R5 = RD2_14_0[5]; R6 = RD2_14_0[6]; R7 = RD2_14_0[7]; R8 = RD2_14_0[8];
  //   R9 = RD2_14_0[9]; R10 = RD2_14_0[10]; R11 = RD2_14_0[11]; R12 = RD2_14_0[12]; R13 = RD2_14_0[13];
  //   R14 = RD2_14_0[14]; RD0 = RD1_14_0[0]; RD1 = RD1_14_0[1]; RD2 = RD1_14_0[2]; RD3 = RD1_14_0[3];
  //   RD4 = RD1_14_0[4]; RD5 = RD1_14_0[5]; RD6 = RD1_14_0[6]; RD7 = RD1_14_0[7]; RD8 = RD1_14_0[8];
  //   RD9 = RD1_14_0[9]; RD10 = RD1_14_0[10]; RD11 = RD1_14_0[11]; RD12 = RD1_14_0[12]; RD13 = RD1_14_0[13];
  //   RD14 = RD1_14_0[14]; WD0 = WD_14_0[0]; WD1 = WD_14_0[1]; WD2 = WD_14_0[2]; WD3 = WD_14_0[3]; WD4 = WD_14_0[4];
  //   WD5 = WD_14_0[5]; WD6 = WD_14_0[6]; WD7 = WD_14_0[7]; WD8 = WD_14_0[8]; WD9 = WD_14_0[9]; WD10 = WD_14_0[10];
  //   WD11 = WD_14_0[11]; WD12 = WD_14_0[12]; WD13 = WD_14_0[13]; WD14 = WD_14_0[14]
endmodule
