// Digital circuit 1 x 4 Register.dig as structural Verilog
module _1_x_4_Register (
  input  [3:0] Din_3_0,
  input  Sel,
  input  Clk,
  output [3:0] Dout_3_0
);

  _1_x_1_Register _1_x_1_register_1 (.Din(Din_3_0[0]), .Sel(Sel), .Clk(Clk), .Dout(Dout_3_0[0]));
  _1_x_1_Register _1_x_1_register_2 (.Din(Din_3_0[1]), .Sel(Sel), .Clk(Clk), .Dout(Dout_3_0[1]));
  _1_x_1_Register _1_x_1_register_3 (.Din(Din_3_0[2]), .Sel(Sel), .Clk(Clk), .Dout(Dout_3_0[2]));
  _1_x_1_Register _1_x_1_register_4 (.Din(Din_3_0[3]), .Sel(Sel), .Clk(Clk), .Dout(Dout_3_0[3]));

  // Other names for the same wires on the sheet: D0 = Din_3_0[0]; D1 = Din_3_0[1]; D2 = Din_3_0[2]; D3 = Din_3_0[3];
  //   R0 = Dout_3_0[0]; R1 = Dout_3_0[1]; R2 = Dout_3_0[2]; R3 = Dout_3_0[3]
endmodule
