// Digital circuit 3 bit PC Adder.dig as structural Verilog
module _3_bit_PC_Adder (
  input  [2:0] I_2_0,
  output [2:0] _0_2_0
);

  Add #(.Bits(3)) add_1 (.a(I_2_0), .b(3'b001), .c_i(1'b0), .s(_0_2_0));  // open: c_o
endmodule
