// Digital circuit 3 bit Program Counter Register.dig as structural Verilog
module _3_bit_Program_Counter_Register (
  input  [2:0] I_2_0,
  input  Clk,
  output [2:0] O_2_0
);

  _1_x_1_Register _1_x_1_register_1 (.Din(I_2_0[0]), .Sel(1'b1), .Clk(Clk), .Dout(O_2_0[0]));
  _1_x_1_Register _1_x_1_register_2 (.Din(I_2_0[1]), .Sel(1'b1), .Clk(Clk), .Dout(O_2_0[1]));
  _1_x_1_Register _1_x_1_register_3 (.Din(I_2_0[2]), .Sel(1'b1), .Clk(Clk), .Dout(O_2_0[2]));

  // Other names for the same wires on the sheet: D0 = I_2_0[0]; D1 = I_2_0[1]; D2 = I_2_0[2]; R0 = O_2_0[0];
  //   R1 = O_2_0[1]; R2 = O_2_0[2]
endmodule
