// Digital circuit 4 bit Adder.dig as structural Verilog
module _4_bit_Adder (
  input  [3:0] A_3_0,
  input  [3:0] B_3_0,
  output [3:0] R_3_0,
  output Cout
);

  wire fa_2_cout, fa_3_cout, fa_4_cout;

  FA fa_1 (.X(B_3_0[3]), .Y(A_3_0[3]), .S(R_3_0[3]), .Cin(fa_2_cout), .Cout(Cout));
  FA fa_2 (.X(B_3_0[2]), .Y(A_3_0[2]), .S(R_3_0[2]), .Cin(fa_3_cout), .Cout(fa_2_cout));
  FA fa_3 (.X(B_3_0[1]), .Y(A_3_0[1]), .S(R_3_0[1]), .Cin(fa_4_cout), .Cout(fa_3_cout));
  FA fa_4 (.X(B_3_0[0]), .Y(A_3_0[0]), .S(R_3_0[0]), .Cin(1'b0), .Cout(fa_4_cout));
endmodule
