// Digital circuit 4 bit XOR.dig as structural Verilog
module _4_bit_XOR (
  input  [3:0] A_3_0,
  input  [3:0] B_3_0,
  output [3:0] R_3_0
);

  xor xor_1 (R_3_0[0], A_3_0[0], B_3_0[0]);
  xor xor_2 (R_3_0[1], A_3_0[1], B_3_0[1]);
  xor xor_3 (R_3_0[2], A_3_0[2], B_3_0[2]);
  xor xor_4 (R_3_0[3], A_3_0[3], B_3_0[3]);
endmodule
