// Digital circuit 4 x 4 Registerset.dig as structural Verilog
module _4_x_4_Registerset (
  input  WE,
  input  [3:0] WRD_3_0,
  input  [1:0] RA_1_0,
  input  [1:0] RB_1_0,
  input  [1:0] WR_1_0,
  input  Clk,
  output [3:0] A_3_0,
  output [3:0] B_3_0
);

  wire A0, A1, A2, A3, D0, D1, D2, D3;
  wire [3:0] R0, R1, R2, R3;

  Decoder #(.Selector_Bits(2)) decoder_1 (.sel(WR_1_0), .out_0(A0), .out_1(A1), .out_2(A2), .out_3(A3));
  and and_1 (D0, WE, A0);
  and and_2 (D1, WE, A1);
  and and_3 (D2, WE, A2);
  and and_4 (D3, WE, A3);
  _1_x_4_Register _1_x_4_register_1 (.Din_3_0(WRD_3_0), .Sel(D3), .Clk(Clk), .Dout_3_0(R3));
  _1_x_4_Register _1_x_4_register_2 (.Din_3_0(WRD_3_0), .Sel(D2), .Clk(Clk), .Dout_3_0(R2));
  _1_x_4_Register _1_x_4_register_3 (.Din_3_0(WRD_3_0), .Sel(D1), .Clk(Clk), .Dout_3_0(R1));
  _1_x_4_Register _1_x_4_register_4 (.Din_3_0(WRD_3_0), .Sel(D0), .Clk(Clk), .Dout_3_0(R0));
  Multiplexer #(.Selector_Bits(2), .Bits(4)) multiplexer_1 (
    .sel(RA_1_0), .in_0(R0), .in_1(R1), .in_2(R2), .in_3(R3), .out(A_3_0));
  Multiplexer #(.Selector_Bits(2), .Bits(4)) multiplexer_2 (
    .sel(RB_1_0), .in_0(R0), .in_1(R1), .in_2(R2), .in_3(R3), .out(B_3_0));
endmodule
