// Digital circuit 7 x 15 RAM.dig as structural Verilog
module _7_x_15_RAM (
  input  [2:0] RA_2_0,
  input  [2:0] RB_2_0,
  input  [2:0] WR_2_0,
  input  [14:0] WD_14_0,
  input  WE,
  input  Clk,
  output [14:0] RD1_14_0,
  output [14:0] RD2_14_0
);

  wire B0, B1, B2, B3, B4, B5, B6, R0, R1, R2, R3, R4, R5, R6, W0, W1, W2, W3, W4, W5, W6;
  wire [14:0] _1_x_15_ram_1_rd1_14_0, _1_x_15_ram_2_rd1_14_0, _1_x_15_ram_3_rd1_14_0, _1_x_15_ram_4_rd1_14_0,
       _1_x_15_ram_5_rd1_14_0, _1_x_15_ram_6_rd1_14_0, _1_x_15_ram_7_rd1_14_0, A0, A1, A2, A3, A4, A5, A6,
       or_1_out, or_2_out, or_3_out, or_4_out;

  Demultiplexer #(.Selector_Bits(3)) demultiplexer_1 (
    .sel(WR_2_0), .in(WE), .out_0(W0), .out_1(W1), .out_2(W2), .out_3(W3), .out_4(W4), .out_5(W5), .out_6(W6));  // open: out_7
  Decoder #(.Selector_Bits(3)) decoder_1 (
    .sel(RA_2_0), .out_0(R0), .out_1(R1), .out_2(R2), .out_3(R3), .out_4(R4), .out_5(R5), .out_6(R6));  // open: out_7
  Decoder #(.Selector_Bits(3)) decoder_2 (
    .sel(RB_2_0), .out_0(B0), .out_1(B1), .out_2(B2), .out_3(B3), .out_4(B4), .out_5(B5), .out_6(B6));  // open: out_7
  _1_x_15_RAM _1_x_15_ram_1 (
    .RS1(R0), .RS2(B0), .WS(W0), .WD_14_0(WD_14_0), .Clk(Clk), .RD1_14_0(_1_x_15_ram_1_rd1_14_0),
    .RD2_14_0(A0));
  _1_x_15_RAM _1_x_15_ram_2 (
    .RS1(R1), .RS2(B1), .WS(W1), .WD_14_0(WD_14_0), .Clk(Clk), .RD1_14_0(_1_x_15_ram_2_rd1_14_0),
    .RD2_14_0(A1));
  _1_x_15_RAM _1_x_15_ram_3 (
    .RS1(R2), .RS2(B2), .WS(W2), .WD_14_0(WD_14_0), .Clk(Clk), .RD1_14_0(_1_x_15_ram_3_rd1_14_0),
    .RD2_14_0(A2));
  _1_x_15_RAM _1_x_15_ram_4 (
    .RS1(R3), .RS2(B3), .WS(W3), .WD_14_0(WD_14_0), .Clk(Clk), .RD1_14_0(_1_x_15_ram_4_rd1_14_0),
    .RD2_14_0(A3));
  _1_x_15_RAM _1_x_15_ram_5 (
    .RS1(R4), .RS2(B4), .WS(W4), .WD_14_0(WD_14_0), .Clk(Clk), .RD1_14_0(_1_x_15_ram_5_rd1_14_0),
    .RD2_14_0(A4));
  _1_x_15_RAM _1_x_15_ram_6 (
    .RS1(R5), .RS2(B5), .WS(W5), .WD_14_0(WD_14_0), .Clk(Clk), .RD1_14_0(_1_x_15_ram_6_rd1_14_0),
    .RD2_14_0(A5));
  _1_x_15_RAM _1_x_15_ram_7 (
    .RS1(R6), .RS2(B6), .WS(W6), .WD_14_0(WD_14_0), .Clk(Clk), .RD1_14_0(_1_x_15_ram_7_rd1_14_0),
    .RD2_14_0(A6));
  assign or_1_out = _1_x_15_ram_1_rd1_14_0 | _1_x_15_ram_2_rd1_14_0 | _1_x_15_ram_3_rd1_14_0 | _1_x_15_ram_4_rd1_14_0 | _1_x_15_ram_5_rd1_14_0;  // Or or_1, 15 bits wide
  assign or_2_out = _1_x_15_ram_6_rd1_14_0 | _1_x_15_ram_7_rd1_14_0;  // Or or_2, 15 bits wide
  assign or_3_out = A0 | A1 | A2 | A3 | A4;  // Or or_3, 15 bits wide
  assign or_4_out = A5 | A6;  // Or or_4, 15 bits wide
  assign RD1_14_0 = or_1_out | or_2_out;  // Or or_5, 15 bits wide
  assign RD2_14_0 = or_3_out | or_4_out;  // Or or_6, 15 bits wide

  // Notes on the sheet:
  //   1x8 DeMux
endmodule
