// Digital circuit CPU.dig as structural Verilog
module CPU (
  input  [2:0] WR_2_0,
  input  [14:0] WD_14_0,
  input  WE,
  input  PC_en,
  input  Clk,
  input  [2:0] RB,
  output [14:0] RD2,
  output [3:0] OPcode,
  output [1:0] OP,
  output [1:0] RA,
  output [1:0] RB_2,
  output [3:0] A,
  output [3:0] B,
  output Imm_Sel,
  output REG_En,
  output JMP_EN,
  output [3:0] R,
  output CF,
  output [3:0] Const,
  output [2:0] JMP_Address
);

  wire CPU_Clk;
  wire [2:0] _3_bit_pc_adder_1__0_2_0, _3_bit_program_counter_register_1_o_2_0, multiplexer_1_out;
  wire [3:0] multiplexer_2_out;
  wire [4:0] Don_t__Care;

  Multiplexer #(.Bits(3)) multiplexer_1 (
    .sel(JMP_EN), .in_0(_3_bit_pc_adder_1__0_2_0), .in_1({JMP_Address[2:1], Const[3]}),
    .out(multiplexer_1_out));
  _3_bit_Program_Counter_Register _3_bit_program_counter_register_1 (
    .I_2_0(multiplexer_1_out), .Clk(CPU_Clk), .O_2_0(_3_bit_program_counter_register_1_o_2_0));
  _3_bit_PC_Adder _3_bit_pc_adder_1 (
    .I_2_0(_3_bit_program_counter_register_1_o_2_0), ._0_2_0(_3_bit_pc_adder_1__0_2_0));
  and and_1 (CPU_Clk, PC_en, Clk);
  _7_x_15_RAM _7_x_15_ram_1 (
    .RA_2_0(_3_bit_program_counter_register_1_o_2_0), .RB_2_0(RB), .WR_2_0(WR_2_0), .WD_14_0(WD_14_0),
    .WE(WE), .Clk(Clk), .RD1_14_0({OPcode, JMP_Address[2:1], Const, Don_t__Care}), .RD2_14_0(RD2));
  _4_x_4_Registerset _4_x_4_registerset_1 (
    .WRD_3_0(R), .WE(REG_En), .RA_1_0(JMP_Address[2:1]), .RB_1_0(Const[3:2]), .WR_1_0(JMP_Address[2:1]),
    .Clk(CPU_Clk), .A_3_0(A), .B_3_0(B));
  _4_bit_ALU _4_bit_alu_1 (.A_3_0(A), .B_3_0(multiplexer_2_out), .R_3_0(R), .OP_1_0(OP), .CF(CF));
  Multiplexer #(.Bits(4)) multiplexer_2 (.sel(Imm_Sel), .in_0(B), .in_1(Const), .out(multiplexer_2_out));
  Control_Circuit control_circuit_1 (
    .Opcode(OPcode), .CF(CF), .Imm_Sel(Imm_Sel), .Reg_En(REG_En), .Op(OP), .Jmp_en(JMP_EN));

  assign JMP_Address[0] = Const[3];
  assign RA = JMP_Address[2:1];
  assign RB_2 = Const[3:2];

  // Other names for the same wires on the sheet: Don_t_Care[7:0] = {Const[2:0], Don_t__Care};
  //   Don_t_Care_t[4:0] = Don_t__Care; Don_t__Care[6:5] = Const[1:0]; RB_t[1:0] = Const[3:2]

  // Notes on the sheet:
  //   Mode Bit(2)    OP Code(2)       RA1         RA2      Don't Care
  //   Register Mode    :     0   0             0   0   (ADD)        2 bit         2bit            7 bit
  //   		   0   1   (Xor)
  //   		   1   0   (ROL)
  //          	      Mode Bit(2)    OP Code(2)       RA1         COnst     Don't Care
  //   Immidiate Mode    :     0   0             0   0   (ADD)       2 bit       4 bit            5 bit
  //   		      0   1   (Xor)
  //   		      1   0   (ROL)
  //   	      Mode Bit(2)    OP Code(2)       RAM_Address     Don't Care
  //   J u m p    M o d e:     1   0                0    0   (JC)               3 bit                  8 bit
endmodule
