// Digital circuit Control Circuit.dig as structural Verilog
module Control_Circuit (
  input  [3:0] Opcode,
  input  CF,
  output Imm_Sel,
  output Reg_En,
  output [1:0] Op,
  output Jmp_en
);

  wire and_2_out, not_1_out, not_2_out;

  not not_1 (not_1_out, Opcode[1]);
  not not_2 (not_2_out, Opcode[0]);
  and and_1 (Imm_Sel, Opcode[0], not_1_out);
  and and_2 (and_2_out, not_2_out, Opcode[1]);
  not not_3 (Reg_En, and_2_out);
  and and_3 (Jmp_en, and_2_out, CF);

  assign Op = Opcode[3:2];

  // Notes on the sheet:
  //   Imm
  //   JMP
endmodule
